// Logisim project Regfile.circ as structural Verilog: 1 circuit, main circuit main
module main (
  input  [1:0] Read_register_1,
  input  [1:0] Read_register_2,
  input  [1:0] write_register,
  input  [15:0] write_data,
  input  RegWrite,
  input  clock,
  output [15:0] Reg_0_Value,
  output [15:0] Reg_1_Value,
  output [15:0] Reg_2_Value,
  output [15:0] Reg_3_Value,
  output [15:0] Read_Data_1,
  output [15:0] Read_Data_2
);

  wire Clock_t, demultiplexer_2_out0, demultiplexer_2_out1, demultiplexer_2_out2, demultiplexer_2_out3,
       Enable0, Enable1, Enable2, Enable3;
  wire [15:0] demultiplexer_1_out0, demultiplexer_1_out1, demultiplexer_1_out2, demultiplexer_1_out3;

  Register #(.width(16)) register_1 (
    .D(demultiplexer_1_out0), .en(Enable0), .Q(Reg_0_Value), .clk(Clock_t));  // open: clr
  Register #(.width(16)) register_2 (
    .D(demultiplexer_1_out1), .en(Enable1), .Q(Reg_1_Value), .clk(Clock_t));  // open: clr
  Demultiplexer #(.select(2), .width(16)) demultiplexer_1 (
    .out0(demultiplexer_1_out0), .out1(demultiplexer_1_out1), .out2(demultiplexer_1_out2),
    .out3(demultiplexer_1_out3), .in(write_data), .sel(write_register));  // open: en
  Register #(.width(16)) register_3 (
    .D(demultiplexer_1_out2), .en(Enable2), .Q(Reg_2_Value), .clk(Clock_t));  // open: clr
  Clock clock_1 (.out(Clock_t));
  Register #(.width(16)) register_4 (
    .D(demultiplexer_1_out3), .en(Enable3), .Q(Reg_3_Value), .clk(Clock_t));  // open: clr
  Multiplexer #(.select(2), .width(16)) multiplexer_1 (
    .in0(Reg_0_Value), .in1(Reg_1_Value), .in2(Reg_2_Value), .in3(Reg_3_Value), .out(Read_Data_1),
    .sel(Read_register_1));  // open: en
  Multiplexer #(.select(2), .width(16)) multiplexer_2 (
    .in0(Reg_0_Value), .in1(Reg_1_Value), .in2(Reg_2_Value), .in3(Reg_3_Value), .out(Read_Data_2),
    .sel(Read_register_2));  // open: en
  Demultiplexer #(.select(2)) demultiplexer_2 (
    .out0(demultiplexer_2_out0), .out1(demultiplexer_2_out1), .out2(demultiplexer_2_out2),
    .out3(demultiplexer_2_out3), .in(1'b1), .sel(write_register));  // open: en
  and and_1 (Enable0, demultiplexer_2_out0, RegWrite);
  and and_2 (Enable1, demultiplexer_2_out1, RegWrite);
  and and_3 (Enable2, demultiplexer_2_out2, RegWrite);
  and and_4 (Enable3, demultiplexer_2_out3, RegWrite);

  // Other names for the same wires on the sheet: Enable = RegWrite; R0[15:0] = Reg_0_Value; R1[15:0] = Reg_1_Value;
  //   R2[15:0] = Reg_2_Value; R3[15:0] = Reg_3_Value; Read1[1:0] = Read_register_1; Read2[1:0] = Read_register_2;
  //   Write_Loc[1:0] = write_register

  // Notes on the sheet:
  //   These are INPUTS to the circuit
  //   These are INPUTS to the circuit
  //   DO NOT CHANGE THE LOCATIONS OF THE INPUTS/OUTPUTS! IF YOU DO SO, YOU NEED TO MAKE SURE THE PINS ARE AT THE RIGHT PLACE!
  //   These are OUTPUTS to the circuit
  //   Yet again, the clock is not an actual clock, but an input, one that will be driven from a higher circuit
  //   These are OUTPUTS to the circuit
endmodule
