// Logisim project alu.circ as structural Verilog: 1 circuit, main circuit main
module main (
  input  [15:0] X,
  input  [15:0] Y,
  input  [3:0] Switch__S,
  output Signed_Overflow,
  output [15:0] RESULT,
  output Equal
);

  wire Over1, Over2, Over3, Over4, Over5, Over6;
  wire [0:0] Out5;
  wire [15:0] Out0, Out1, Out2, Out3, Out4, Out6, Out7, Out8, Out9;
  wire [31:0] add, addp8, \and , demultiplexer_1_out10, demultiplexer_1_out11, demultiplexer_1_out12,
       demultiplexer_1_out13, demultiplexer_1_out14, demultiplexer_1_out15, \or , sllv, slt, srav, srlv, sub,
       subp8;

  Adder #(.width(16)) adder_1 (.a(add[15:0]), .b(add[31:16]), .out(Out0), .cout(Over1));  // open: cin
  Subtractor #(.width(16)) subtractor_1 (.a(sub[15:0]), .b(sub[31:16]), .out(Out1), .bout(Over2));  // open: bin
  Shifter #(.width(16)) shifter_1 (.in(sllv[15:0]), .\dist (sllv[19:16]), .out(Out2));
  Shifter #(.width(16), .shift("lr")) shifter_2 (.in(srlv[15:0]), .\dist (srlv[19:16]), .out(Out3));
  Demultiplexer #(.select(4), .width(32)) demultiplexer_1 (
    .out0(add), .out1(sub), .out2(sllv), .out3(srlv), .out4(srav), .out5(slt), .out6(\or ), .out7(\and ),
    .out8(addp8), .out9(subp8), .out10(demultiplexer_1_out10), .out11(demultiplexer_1_out11),
    .out12(demultiplexer_1_out12), .out13(demultiplexer_1_out13), .out14(demultiplexer_1_out14),
    .out15(demultiplexer_1_out15), .in({Y, X}), .sel(Switch__S));  // open: en
  Shifter #(.width(16), .shift("ar")) shifter_3 (.in(srav[15:0]), .\dist (srav[19:16]), .out(Out4));
  Comparator #(.width(16)) comparator_1 (.a(slt[15:0]), .b(slt[31:16]), .lt(Out5[0]));  // open: gt, eq
  assign Out6 = \or [15:0] | \or [31:16];  // OR_Gate or_1, 16 bits wide
  assign Out7 = \and [15:0] & \and [31:16];  // AND_Gate and_1, 16 bits wide
  Comparator #(.width(16)) comparator_2 (.a(X), .b(Y), .eq(Equal));  // open: gt, lt
  Adder adder_2 (.a(addp8[7:0]), .b(addp8[23:16]), .out(Out8[7:0]), .cout(Over3));  // open: cin
  Adder adder_3 (.a(addp8[15:8]), .b(addp8[31:24]), .out(Out8[15:8]), .cout(Over4));  // open: cin
  Subtractor subtractor_2 (.a(subp8[7:0]), .b(subp8[23:16]), .out(Out9[7:0]), .bout(Over5));  // open: bin
  Subtractor subtractor_3 (.a(subp8[15:8]), .b(subp8[31:24]), .out(Out9[15:8]), .bout(Over6));  // open: bin
  or or_2 (Signed_Overflow, Over1, Over2, Over3, Over4, Over5, Over6);
  assign RESULT = Out0 | Out1 | Out2 | Out3 | Out4 | {{15{1'b0}}, Out5[0]} | Out6 | Out7 | Out8 | Out9;  // OR_Gate or_3, 16 bits wide

  // Other names for the same wires on the sheet: Out[15:0] = RESULT; Over = Signed_Overflow

  // Notes on the sheet:
  //   INPUTS to your circuit
  //   INPUT to your circuit
  //   DON'T CHANGE THE INPUTS AND OUTPUTS! IF YOU DO SO, YOU NEED TO MAKE SURE THE PINS ARE IN THE RIGHT PLACES!
  //   OUTPUTS of your circuit
endmodule
