// Logisim project cpu.circ as structural Verilog: 10 circuits, main circuit main
module main (
  input  [15:0] From_Instr_Mem,
  input  clk,
  output [15:0] r0,
  output [15:0] r1,
  output [15:0] r2,
  output [15:0] r3,
  output [15:0] Display_0,
  output [15:0] Display_1,
  output [15:0] To_Instr_Mem,
  output [15:0] Data_Mem_Data,
  output [15:0] Data_Mem_Addr,
  output Data_Mem_Write
);

  wire and_1_out, and_2_out, branchtype, comparator_4_eq, comparator_5_eq, display0control, display1control,
       Display_Control, equalouts, killnextinstruction, not_1_out, not_2_out, or_2_out, overflow, RegWrite,
       rtype;
  wire [1:0] multiplexer_4_out, pc_control, rd, Register_Write_Control_register_data_selector, rs, rt,
       signextendcontrol_1_sign_extend, writeregister;
  wire [3:0] multiplexer_6_out, op_to_func_funct, opcode;
  wire [5:0] funct;
  wire [7:0] offset_immediate;
  wire [11:0] target_addr;
  wire [15:0] adder_1_out, ALU_in_1, ALU_in_2, Counter, DataIn, extended_immediate, jump_address,
       multiplexer_1_out, multiplexer_2_out, multiplexer_3_out, register_1_q, Result;

  Counter #(.width(16), .max('hffff)) counter_1 (.Q(Counter), .clk(clk));  // open: load, D, count, carry, clr
  Multiplexer #(.width(16)) multiplexer_1 (
    .in0(From_Instr_Mem), .in1(16'h6), .out(multiplexer_1_out), .sel(killnextinstruction));  // open: en
  Adder #(.width(16)) adder_1 (.a(To_Instr_Mem), .b(16'h1), .out(adder_1_out));  // open: cin, cout
  // Probe on jump_address
  InstDecode Inst_Decode (
    .Inst(register_1_q), .funct(funct), .rd(rd), .rt(rt), .rs(rs), .target_address(target_addr),
    .offset_immediate(offset_immediate), .opcode(opcode));
  Register #(.width(16)) register_1 (.D(multiplexer_1_out), .Q(register_1_q), .clk(clk));  // open: en, clr
  Multiplexer #(.select(2), .width(16)) multiplexer_2 (
    .in0({16{1'b0}}), .in1(adder_1_out), .in2(jump_address), .out(multiplexer_2_out), .sel(pc_control));  // open: in3, en
  Comparator #(.width(16), .mode("unsigned")) comparator_1 (
    .a(extended_immediate), .b({16{1'b0}}), .eq(display0control));  // open: gt, lt
  Comparator #(.width(16), .mode("unsigned")) comparator_2 (
    .a(extended_immediate), .b(16'h1), .eq(display1control));  // open: gt, lt
  // Probe on rt
  // Probe on opcode
  // Probe on rs
  Register #(.width(16)) PC (.D(multiplexer_2_out), .Q(To_Instr_Mem), .clk(clk), .clr(1'b0));  // open: en
  // Probe on From_Instr_Mem
  // Probe on rd
  // Probe on To_Instr_Mem
  // Probe on funct
  // Probe on target_addr
  // Probe on offset_immediate
  signextendcontrol signextendcontrol_1 (.opcode(opcode), .Sign_Extend(signextendcontrol_1_sign_extend));
  Multiplexer #(.select(2), .width(16)) multiplexer_3 (
    .in0(Result), .in1(extended_immediate), .in2(Data_Mem_Data), .in3(To_Instr_Mem), .out(multiplexer_3_out),
    .sel(Register_Write_Control_register_data_selector));  // open: en
  Register_Write_Data_Control Register_Write_Control (
    .Opcode(opcode), .Register_Data_Selector(Register_Write_Control_register_data_selector));
  signExtender ImmediateExtender (
    .Immediate(offset_immediate), .Sign_Extend(signextendcontrol_1_sign_extend),
    .Extended_Immediate(extended_immediate));
  writeregcontrol Write_Register_Selector (.opcode(opcode), .writeregister(writeregister));
  registerwritecontrol Register_Write_Boolean (.opcode(opcode), .Register_Write(RegWrite));
  Comparator #(.width(4), .mode("unsigned")) comparator_3 (.a(opcode), .b(4'b0000), .eq(rtype));  // open: gt, lt
  Comparator #(.width(4), .mode("unsigned")) comparator_4 (
    .a(opcode), .b(4'b0100), .eq(comparator_4_eq));  // open: gt, lt
  Comparator #(.width(4), .mode("unsigned")) comparator_5 (
    .a(opcode), .b(4'b1000), .eq(comparator_5_eq));  // open: gt, lt
  Comparator #(.width(4), .mode("unsigned")) comparator_6 (
    .a(opcode), .b(4'b1100), .eq(Display_Control));  // open: gt, lt
  Comparator #(.width(4), .mode("unsigned")) comparator_7 (
    .a(opcode), .b(4'b1001), .eq(Data_Mem_Write));  // open: gt, lt
  pc_control PC_Controller (.opcode(opcode), .registersequal(equalouts), .counter(Counter), .PC_controller(pc_control));
  // Probe on rs
  // Probe on rt
  // Probe on multiplexer_4_out
  Multiplexer #(.select(2), .width(2)) multiplexer_4 (
    .in0(rt), .in1(rd), .in2(2'b11), .out(multiplexer_4_out), .sel(writeregister));  // open: in3, en
  // Probe on Register_Write_Control_register_data_selector
  // Probe on extended_immediate
  or or_1 (branchtype, comparator_4_eq, comparator_5_eq);
  // Probe on multiplexer_3_out
  Regfile_main Register_File (
    .Read_register_1(rs), .Read_register_2(rt), .write_register(multiplexer_4_out),
    .write_data(multiplexer_3_out), .Reg_0_Value(r0), .Reg_1_Value(r1), .Reg_2_Value(r2), .Reg_3_Value(r3),
    .RegWrite(RegWrite), .clock(clk), .Read_Data_1(ALU_in_1), .Read_Data_2(DataIn));
  // Probe on ALU_in_1
  // Probe on DataIn
  Comparator #(.width(2)) comparator_8 (.a(pc_control), .b(2'b10), .eq(killnextinstruction));  // open: gt, lt
  or or_2 (or_2_out, rtype, branchtype);
  Adder #(.width(16)) adder_2 (.a(ALU_in_1), .b(extended_immediate), .out(Data_Mem_Addr));  // open: cin, cout
  Jump_Address_Determine Jump_Find (
    .Opcode(opcode), .Target_Address(target_addr), .PC_in(To_Instr_Mem), .Jump_Register(ALU_in_1),
    .Signed_Offset(extended_immediate), .Jump_Address__PC_Out(jump_address));
  Hex_Digit_Display hex_digit_display_1 (.value(Display_0[15:12]));  // open: dp
  Multiplexer #(.width(16)) multiplexer_5 (
    .in0(extended_immediate), .in1(DataIn), .out(ALU_in_2), .sel(or_2_out));  // open: en
  Hex_Digit_Display hex_digit_display_2 (.value(Display_0[11:8]));  // open: dp
  Hex_Digit_Display hex_digit_display_3 (.value(Display_0[7:4]));  // open: dp
  // Probe on funct[3:0]
  and and_1 (and_1_out, display0control, Display_Control);
  and and_2 (and_2_out, display1control, Display_Control);
  Hex_Digit_Display hex_digit_display_4 (.value(Display_0[3:0]));  // open: dp
  alu_main ALU (
    .Switch__S(multiplexer_6_out), .X(ALU_in_1), .Equal(equalouts), .RESULT(Result),
    .Signed_Overflow(overflow), .Y(ALU_in_2));
  Multiplexer #(.width(4)) multiplexer_6 (
    .in0(funct[3:0]), .in1(op_to_func_funct), .out(multiplexer_6_out), .sel(not_1_out));  // open: en
  not not_1 (not_1_out, rtype);
  RAM #(.addrWidth(16), .dataWidth(16)) ram_1 (
    .addr(Data_Mem_Addr), .data(Data_Mem_Data), .sel(1'b1), .clk(clk), .ld(not_2_out), .clr(1'b0));
  not not_2 (not_2_out, Data_Mem_Write);
  Register #(.width(16)) register_2 (.D(ALU_in_1), .en(and_1_out), .Q(Display_0), .clk(clk));  // open: clr
  Register #(.width(16)) register_3 (.D(ALU_in_1), .en(and_2_out), .Q(Display_1), .clk(clk));  // open: clr
  Hex_Digit_Display hex_digit_display_5 (.value(Display_1[15:12]));  // open: dp
  Hex_Digit_Display hex_digit_display_6 (.value(Display_1[11:8]));  // open: dp
  // Probe on Result
  // Probe on op_to_func_funct
  opcontrol op_to_func (.Opcode(opcode), .Funct(op_to_func_funct));
  // Probe on DataIn
  assign Data_Mem_Data = Data_Mem_Write ? DataIn : 16'bz;  // Controlled_Buffer controlled_buffer_1
  Hex_Digit_Display hex_digit_display_7 (.value(Display_1[3:0]));  // open: dp
  Hex_Digit_Display hex_digit_display_8 (.value(Display_1[7:4]));  // open: dp
  LED led_1 (.in(overflow));
  // Probe on opcode
  // Probe on Data_Mem_Data

  // Other names for the same wires on the sheet: d0[15:0] = Display_0; d1[15:0] = Display_1;
  //   Data_Address[15:0] = Data_Mem_Addr; DataWrite = Data_Mem_Write; Instruction[15:0] = From_Instr_Mem;
  //   pc[15:0] = To_Instr_Mem; rout1[15:0] = ALU_in_1; rout2[15:0] = DataIn

  // Notes on the sheet:
  //   This is the current PC that you need to send as OUTPUT
  //   This is the instruction that you would receive as INPUT
  //   This is a CLK that is an INPUT driven from the harness.
  //   Remember, this circuit is loaded from the harness to be tested!
  //   DO NOT CHANGE THE LOCATIONS OF THE INPUTS OR OUTPUTS! IF YOU DO SO, YOU NEED TO MAKE SURE THE PINS ARE IN THE RIGHT PLACES!
  //   These are OUTPUTS of the circuit
  //   These are OUTPUTS of the circuit
endmodule

module InstDecode (
  input  [15:0] Inst,
  output [5:0] funct,
  output [1:0] rd,
  output [1:0] rt,
  output [1:0] rs,
  output [11:0] target_address,
  output [7:0] offset_immediate,
  output [3:0] opcode
);

  wire [11:0] demultiplexer_1_out1, demultiplexer_1_out2, demultiplexer_1_out3, demultiplexer_1_out4,
       demultiplexer_1_out5, demultiplexer_1_out6, demultiplexer_1_out7, demultiplexer_1_out8,
       demultiplexer_1_out9, demultiplexer_1_out10, demultiplexer_1_out11, demultiplexer_1_out12;
  wire [11:8] demultiplexer_1_out0, multiplexer_1_out;

  Demultiplexer #(.select(4), .width(12)) demultiplexer_1 (
    .out0({demultiplexer_1_out0, rd, funct}), .out1(demultiplexer_1_out1), .out2(demultiplexer_1_out2),
    .out3(demultiplexer_1_out3), .out4(demultiplexer_1_out4), .out5(demultiplexer_1_out5),
    .out6(demultiplexer_1_out6), .out7(demultiplexer_1_out7), .out8(demultiplexer_1_out8),
    .out9(demultiplexer_1_out9), .out10(demultiplexer_1_out10), .out11(demultiplexer_1_out11),
    .out12(demultiplexer_1_out12), .in(Inst[11:0]), .sel(Inst[15:12]));  // open: out13, out14, out15, en
  Multiplexer #(.select(4), .width(12)) multiplexer_1 (
    .in0({12{1'b0}}), .in1({12{1'b0}}), .in2({12{1'b0}}), .in3({12{1'b0}}), .in4(demultiplexer_1_out4),
    .in5(demultiplexer_1_out5), .in6(demultiplexer_1_out6), .in7(demultiplexer_1_out7),
    .in8(demultiplexer_1_out8), .in9(demultiplexer_1_out9), .in10(demultiplexer_1_out10),
    .in11(demultiplexer_1_out11), .in12(demultiplexer_1_out12), .in13({12{1'b0}}), .in14({12{1'b0}}),
    .in15({12{1'b0}}), .out({multiplexer_1_out, offset_immediate}), .sel(Inst[15:12]));  // open: en
  assign rt = demultiplexer_1_out0[9:8] | multiplexer_1_out[9:8];  // OR_Gate or_1, 2 bits wide
  assign rs = demultiplexer_1_out0[11:10] | demultiplexer_1_out3[11:10] | multiplexer_1_out[11:10];  // OR_Gate or_2, 2 bits wide
  assign target_address = demultiplexer_1_out1 | demultiplexer_1_out2;  // OR_Gate or_3, 12 bits wide

  assign opcode = Inst[15:12];
endmodule

module signExtender (
  input  [7:0] Immediate,
  input  [1:0] Sign_Extend,
  output [15:0] Extended_Immediate
);

  wire [8:0] multiplexer_1_out;

  // Probe on Immediate
  // Probe on Immediate
  Multiplexer #(.width(9)) multiplexer_1 (
    .in0({9{1'b0}}), .in1({9{1'b1}}), .out(multiplexer_1_out), .sel(Immediate[7]));  // open: en
  Multiplexer #(.select(2), .width(16)) multiplexer_2 (
    .in0({{8{1'b0}}, Immediate}), .in1({multiplexer_1_out, Immediate[6:0]}), .in2({Immediate, {8{1'b0}}}),
    .out(Extended_Immediate), .sel(Sign_Extend));  // open: in3, en
  // Probe on Extended_Immediate
  // Probe on Extended_Immediate

  // Notes on the sheet:
  //   0, no sign extend, 1 sign extend, 2 shift right 8
endmodule

module opcontrol (
  input  [3:0] Opcode,
  output [3:0] Funct
);

  wire comparator_1_eq, comparator_1_gt, comparator_1_lt;
  wire [1:0] multiplexer_1_out, undriven, undriven_2, undriven_3;

  Comparator #(.width(4), .mode("unsigned")) comparator_1 (
    .a(Opcode), .b(4'b0110), .gt(comparator_1_gt), .eq(comparator_1_eq), .lt(comparator_1_lt));
  Multiplexer #(.width(2)) multiplexer_1 (
    .in0(undriven), .in1(2'b10), .out(multiplexer_1_out), .sel(comparator_1_gt));  // open: en
  Multiplexer #(.select(2), .width(4)) multiplexer_2 (
    .in0(4'b0000), .in1(4'b0111), .in2(4'b0110), .out(Funct), .sel(multiplexer_1_out));  // open: in3, en
  Multiplexer #(.width(2)) multiplexer_3 (
    .in0(undriven_2), .in1(2'b01), .out(multiplexer_1_out), .sel(comparator_1_eq));  // open: en
  Multiplexer #(.width(2)) multiplexer_4 (
    .in0(undriven_3), .in1(2'b00), .out(multiplexer_1_out), .sel(comparator_1_lt));  // open: en
endmodule

module writeregcontrol (
  input  [3:0] opcode,
  output [1:0] writeregister
);

  wire comparator_2_eq;
  wire [0:0] comparator_1_eq;

  Comparator #(.width(4)) comparator_1 (.a(opcode), .b(4'b0000), .eq(comparator_1_eq[0]));  // open: gt, lt
  Comparator #(.width(4), .mode("unsigned")) comparator_2 (
    .a(opcode), .b(4'b0001), .eq(comparator_2_eq));  // open: gt, lt
  Multiplexer #(.width(2)) multiplexer_1 (
    .in0({1'b0, comparator_1_eq[0]}), .in1(2'b10), .out(writeregister), .sel(comparator_2_eq));  // open: en

  // Notes on the sheet:
  //   0 is rt, 1 is rd. 2 is r3
endmodule

module signextendcontrol (
  input  [3:0] opcode,
  output [1:0] Sign_Extend
);

  wire comparator_1_eq, comparator_2_eq, comparator_3_eq, comparator_4_eq, comparator_5_eq, comparator_6_eq;
  wire [0:0] or_1_out;

  Comparator #(.width(4)) comparator_1 (.a(opcode), .b(4'b0100), .eq(comparator_1_eq));  // open: gt, lt
  Comparator #(.width(4)) comparator_2 (.a(opcode), .b(4'b0101), .eq(comparator_2_eq));  // open: gt, lt
  Comparator #(.width(4)) comparator_3 (.a(opcode), .b(4'b1000), .eq(comparator_3_eq));  // open: gt, lt
  Comparator #(.width(4)) comparator_4 (.a(opcode), .b(4'b1001), .eq(comparator_4_eq));  // open: gt, lt
  Comparator #(.width(4)) comparator_5 (.a(opcode), .b(4'b1011), .eq(comparator_5_eq));  // open: gt, lt
  Comparator #(.width(4)) comparator_6 (.a(opcode), .b(4'b1010), .eq(comparator_6_eq));  // open: gt, lt
  or or_1 (or_1_out[0], comparator_1_eq, comparator_2_eq, comparator_3_eq, comparator_4_eq, comparator_5_eq);
  Multiplexer #(.width(2)) multiplexer_1 (
    .in0({1'b0, or_1_out[0]}), .in1(2'b10), .out(Sign_Extend), .sel(comparator_6_eq));  // open: en

  // Notes on the sheet:
  //   0, no sign extend, 1 sign extend, 2 shift right 8
endmodule

module registerwritecontrol (
  input  [3:0] opcode,
  output Register_Write
);

  wire comparator_1_eq, comparator_2_eq, comparator_3_eq, comparator_4_eq, comparator_5_eq, comparator_6_eq,
       comparator_7_eq;

  Comparator #(.width(4)) comparator_1 (.a(opcode), .b(4'b0000), .eq(comparator_1_eq));  // open: gt, lt
  Comparator #(.width(4)) comparator_2 (.a(opcode), .b(4'b0001), .eq(comparator_2_eq));  // open: gt, lt
  Comparator #(.width(4)) comparator_3 (.a(opcode), .b(4'b0101), .eq(comparator_3_eq));  // open: gt, lt
  Comparator #(.width(4)) comparator_4 (.a(opcode), .b(4'b0110), .eq(comparator_4_eq));  // open: gt, lt
  Comparator #(.width(4)) comparator_5 (.a(opcode), .b(4'b0111), .eq(comparator_5_eq));  // open: gt, lt
  Comparator #(.width(4)) comparator_6 (.a(opcode), .b(4'b1010), .eq(comparator_6_eq));  // open: gt, lt
  Comparator #(.width(4)) comparator_7 (.a(opcode), .b(4'b1011), .eq(comparator_7_eq));  // open: gt, lt
  or or_1 (Register_Write, comparator_1_eq, comparator_2_eq, comparator_3_eq, comparator_4_eq, comparator_5_eq, comparator_6_eq, comparator_7_eq);
endmodule

module Register_Write_Data_Control (
  input  [3:0] Opcode,
  output [1:0] Register_Data_Selector
);

  wire comparator_1_eq, comparator_1_gt, comparator_3_eq;
  wire [0:0] comparator_2_eq, or_1_out;
  wire [1:0] adder_1_out, adder_2_out, adder_3_out;

  Comparator #(.width(4), .mode("unsigned")) comparator_1 (
    .a(Opcode), .b(4'b1010), .gt(comparator_1_gt), .eq(comparator_1_eq));  // open: lt
  Comparator #(.width(4), .mode("unsigned")) comparator_2 (
    .a(Opcode), .b(4'b1011), .eq(comparator_2_eq[0]));  // open: gt, lt
  Comparator #(.width(4), .mode("unsigned")) comparator_3 (
    .a(Opcode), .b(4'b0001), .eq(comparator_3_eq));  // open: gt, lt
  or or_1 (or_1_out[0], comparator_1_gt, comparator_1_eq);
  Adder #(.width(2)) adder_1 (.a(2'b00), .b({1'b0, or_1_out[0]}), .out(adder_1_out));  // open: cin, cout
  Adder #(.width(2)) adder_2 (.a(2'b00), .b({1'b0, comparator_2_eq[0]}), .out(adder_2_out));  // open: cin, cout
  Adder #(.width(2)) adder_3 (.a(adder_1_out), .b(adder_2_out), .out(adder_3_out));  // open: cin, cout
  Multiplexer #(.width(2)) multiplexer_1 (
    .in0(adder_3_out), .in1(2'b11), .out(Register_Data_Selector), .sel(comparator_3_eq));  // open: en
endmodule

module pc_control (
  input  [3:0] opcode,
  input  registersequal,
  input  [15:0] counter,
  output [1:0] PC_controller
);

  wire and_1_out, and_2_out, comparator_1_eq, comparator_1_gt, comparator_2_eq, comparator_3_eq,
       comparator_4_eq, comparator_5_eq, comparator_6_eq, comparator_7_eq, not_1_out;
  wire [0:0] or_1_out, or_2_out;
  wire [1:0] adder_1_out;

  Comparator #(.width(4), .mode("unsigned")) comparator_1 (
    .a(opcode), .b(4'b0000), .gt(comparator_1_gt), .eq(comparator_1_eq));  // open: lt
  Comparator #(.width(4), .mode("unsigned")) comparator_2 (
    .a(opcode), .b(4'b0001), .eq(comparator_2_eq));  // open: gt, lt
  Comparator #(.width(4), .mode("unsigned")) comparator_3 (
    .a(opcode), .b(4'b0010), .eq(comparator_3_eq));  // open: gt, lt
  Comparator #(.width(4), .mode("unsigned")) comparator_4 (
    .a(opcode), .b(4'b0011), .eq(comparator_4_eq));  // open: gt, lt
  Comparator #(.width(4), .mode("unsigned")) comparator_5 (
    .a(opcode), .b(4'b0100), .eq(comparator_5_eq));  // open: gt, lt
  Comparator #(.width(4), .mode("unsigned")) comparator_6 (
    .a(opcode), .b(4'b1000), .eq(comparator_6_eq));  // open: gt, lt
  not not_1 (not_1_out, registersequal);
  or or_1 (or_1_out[0], comparator_1_gt, comparator_1_eq);
  and and_1 (and_1_out, comparator_5_eq, registersequal);
  and and_2 (and_2_out, comparator_6_eq, not_1_out);
  Comparator #(.width(16), .mode("unsigned")) comparator_7 (
    .a(counter), .b({16{1'b0}}), .eq(comparator_7_eq));  // open: gt, lt
  or or_2 (or_2_out[0], comparator_2_eq, comparator_3_eq, comparator_4_eq, and_1_out, and_2_out);
  Adder #(.width(2)) adder_1 (.a({1'b0, or_1_out[0]}), .b({1'b0, or_2_out[0]}), .out(adder_1_out));  // open: cin, cout
  Multiplexer #(.width(2)) multiplexer_1 (
    .in0(adder_1_out), .in1(2'b00), .out(PC_controller), .sel(comparator_7_eq));  // open: en

  // Notes on the sheet:
  //   0 means initialize pc to zero, 1 is increment by 1, 2 is branch or jump
endmodule

module Jump_Address_Determine (
  input  [3:0] Opcode,
  input  [11:0] Target_Address,
  input  [15:0] PC_in,
  input  [15:0] Jump_Register,
  input  [15:0] Signed_Offset,
  output [15:0] Jump_Address__PC_Out
);

  wire [15:0] adder_1_out, adder_2_out;

  Adder #(.width(16)) adder_1 (.a(PC_in), .b({16{1'b0}}), .out(adder_1_out));  // open: cin, cout
  Adder #(.width(16)) adder_2 (.a(adder_1_out), .b(Signed_Offset), .out(adder_2_out));  // open: cin, cout
  Multiplexer #(.select(4), .width(16)) multiplexer_1 (
    .in1({PC_in[15:12], Target_Address}), .in2({PC_in[15:12], Target_Address}), .in3(Jump_Register),
    .in4(adder_2_out), .in8(adder_2_out), .out(Jump_Address__PC_Out), .sel(Opcode));  // open: in0, in5, in6, in7, in9, in10, in11, in12, in13, in14, in15, en
endmodule
